// Logisim project LogismDiagrams.circ as structural Verilog: 1 circuit, main circuit main
module main (
  input  in_1,
  input  in_2,
  input  in_3,
  input  in_4,
  input  in_5,
  input  in_6,
  input  in_7,
  input  a,
  input  b,
  input  sel,
  output out_11,
  output out_12,
  output out_13,
  output out_14,
  output out_15,
  output out_16
);

  wire and_1_out, and_2_out, and_3_out, nand_1_out, nand_2_out, not_1_out, not_2_out, not_3_out, or_1_out;

  not not_1 (not_1_out, in_1);
  not not_2 (not_2_out, in_4);
  or or_1 (or_1_out, in_5, in_6);
  and and_1 (and_1_out, in_7, in_5);
  not not_3 (not_3_out, sel);
  and and_2 (and_2_out, not_1_out, in_4);
  and and_3 (and_3_out, in_1, not_2_out);
  and and_4 (out_13, or_1_out, and_1_out);
  and and_5 (out_14, a, not_3_out);
  and and_6 (out_16, b, sel);
  or or_2 (out_11, and_2_out, and_3_out);
  or or_3 (out_15, out_14, out_16);
  nand nand_1 (nand_1_out, in_2, in_2, in_2);
  nand nand_2 (nand_2_out, in_3, in_3);
  nand nand_3 (out_12, nand_1_out, nand_2_out);

  // Notes on the sheet:
  //   My first XOR
  //   MUX - failed design
  //   MUX attempt #2
  //   OR
endmodule
